# Fritzing sketch WeatherDisplay (saved by Fritzing 0.9.4)

parts:
  Part1 = Adafruit TPL5111 Reset Enable Timer [part_number="Adafruit #3573"]
  Part2 = Adafruit Feather M0 WINC1500 [part_number="Adafruit #3010"]
  Part3 = 2.13in Tri-Color eInk Display [part_number="Adafruit #4086"]

nets:
  N1: Part1.VDD, Part2.VBUS
  GND: Part1.GND, Part2.GND, Part3.GND
  N2: Part1.ENOUT, Part2.EN
  N3: Part1.DONE, Part2.D6
  N4: Part2.MISO, Part3.MISO
  N5: Part2.MOSI, Part3.MOSI
  N6: Part2.SCK, Part3.SCLK
  +3V3: Part2.+3V3, Part3.VIN
  N7: Part2.D13, Part3.DISPCS
  N8: Part2.D12, Part3.DC
  N9: Part2.D11, Part3.SRAMCS
  N10: Part2.D10, Part3.RESET

custom parts:
  Adafruit TPL5111 Reset Enable Timer: The Adafruit TPL5111 Reset Enable Timer is a stand-alone breakout that will turn any electronics into low-power electronics! It will take care of enabling & disabling your electronics using a built in timer that can vary from once-every 100ms up to once every two hours. Basically, the TPL will set an enable pin high periodically, adjustable by potentiometer or resistor, and turn on your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
  Adafruit Feather M0 WINC1500: This is the Adafruit Feather M0 WiFi w/ATWINC1500 - our take on an 'all-in-one' Arduino-compatible + high speed, reliable WiFi with built in USB and battery charging. Its an Adafruit Feather M0 with a WiFi module, ready to rock! Connect your Feather to the Internet with this fine new FCC-certified WiFi module from Atmel. This 802.11bgn-capable WiFi module is the best new thing for networking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
